# Fritzing sketch how-to-button (saved by Fritzing 0.9.3b)
breadboards: 1

parts:
  Part2 = Adafruit Pi Cobbler Plus [part_number="Adafruit #2029"]  # not connected
  R8 = Resistor [tolerance=±5% resistance=220 package="1206 [SMD]"]
  S2 = Momentary Switch [package=ksa_sealed_tac_switch]

nets:
  N1: R8.Pin_0, S2.2

custom parts:
  Adafruit Pi Cobbler Plus: The Raspberry Pi B+/Pi 2/ Pi 3 has landed on the Maker World like a 40-GPIO pinned, quad-USB ported, credit card sized bomb of DIY joy. And while you can use most of our great Model B accessories by hooking up our downgrade cable, its probably a good time to upgrade your set up and accessorize using all of the Model B+'s / Pi 2's / Pi 3's 40 pins. That's why we now carry the Adafruit Assembled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
